# Fritzing sketch Super Maquina (saved by Fritzing 0.9.3b)
circuit board: 7.64511cm x 5.54585cm
breadboards: 1

parts:
  LED1 = LED - 5mm [color="Red (633nm)" package="5 mm [THT]"]
  LED2 = LED - 5mm [color="Red (633nm)" package="5 mm [THT]"]
  LED3 = LED - 5mm [color="Red (633nm)" package="5 mm [THT]"]
  LED4 = LED - 5mm [color="Red (633nm)" package="5 mm [THT]"]
  LED5 = LED - 5mm [color="Red (633nm)" package="5 mm [THT]"]
  R1 = Resistor [tolerance=±5% resistance=220 package=THT]
  R2 = Resistor [tolerance=±5% resistance=220 package=THT]
  R3 = Resistor [tolerance=±5% resistance=220 package=THT]
  R4 = Resistor [tolerance=±5% resistance=220 package=THT]
  R5 = Resistor [tolerance=±5% resistance=220 package=THT]
  Componente1 = Arduino Uno (Rev3)

nets:
  N1: LED1.cathode, R1.Pin_1
  N2: LED1.anode, Componente1.D13/SCK
  N3: LED2.cathode, R2.Pin_1
  N4: LED2.anode, Componente1.D12/MISO
  N5: LED3.cathode, R3.Pin_1
  N6: LED3.anode, Componente1.D11_PWM/MOSI
  N7: LED4.cathode, R4.Pin_1
  N8: LED4.anode, Componente1.D10_PWM/SS
  N9: LED5.cathode, R5.Pin_1
  N10: LED5.anode, Componente1.D9_PWM
  N11: R1.Pin_0, R2.Pin_0, R3.Pin_0, R4.Pin_0, R5.Pin_0, Componente1.GND

// code stored in the sketch: Untitled.ino
/**
 * Efeito Super Maquina
 * @author Leonel Paim
 */
void setup() {
  pinMode(13,OUTPUT);
  pinMode(12,OUTPUT);
  pinMode(11,OUTPUT);
  pinMode(10,OUTPUT);
  pinMode(9,OUTPUT);
}

void loop() {
 int efeito = 100;
 for (int i=13; i>=9; i--){
 digitalWrite (i, HIGH);
 delay(efeito);
 digitalWrite(i, LOW);
 }

 for (int i=10; i<=12; i++){
 digitalWrite (i, HIGH);
 delay(efeito);
 digitalWrite(i, LOW);
}
 }
